# Fritzing sketch V0 DTY MCAS (saved by Fritzing 0.9.3b)
circuit board: 9.65877cm x 6.58367cm
breadboards: 1

parts:
  NANO = Arduino Nano (Rev3.0)
  LED_SON = LED - 5mm [color="Red (633nm)" package="5 mm [THT]"]
  LED_DIST = LED - 5mm [color="Red (633nm)" package="5 mm [THT]"]
  LED_LUX = LED - 5mm [color="Red (633nm)" package="5 mm [THT]"]
  7_SEGMENTS = mystery part, 4 pins [chip_label=?]
  POINTEUR = mystery part, 3 pins [chip_label=?]
  LUX = mystery part, 3 pins [chip_label=?]
  SON = mystery part, 3 pins [chip_label=?]
  BLUETOOTH = mystery part, 4 pins [chip_label=?]
  DIST = mystery part, 4 pins [chip_label=?]
  BATTERIE = Battery
  HP = Microphone
  RBPLAY = Resistor [tolerance=±5% resistance=220 package="1206 [SMD]"]
  RBLUX = Resistor [tolerance=±5% resistance=220 package="1206 [SMD]"]
  RBSON = Resistor [tolerance=±5% resistance=220 package="1206 [SMD]"]
  RLSON = Resistor [tolerance=±5% resistance=220 package="1206 [SMD]"]
  BSON = Tilt Switch [package=THT]
  BDIST = Tilt Switch [package=THT]
  BLUX = Tilt Switch [package=THT]
  BPLAY = Tilt Switch [package=THT]
  RBATTERIE2 = Resistor [tolerance=±5% resistance=220 package="1206 [SMD]"]
  RBATTERIE = Resistor [tolerance=±5% resistance=220 package="1206 [SMD]"]
  RBDIST = Resistor [tolerance=±5% resistance=220 package="1206 [SMD]"]
  RLLUX = Resistor [tolerance=±5% resistance=220 package="1206 [SMD]"]

nets:
  GND: NANO.GND, LED_DIST.anode, 7_SEGMENTS.pin1, POINTEUR.pin3, LUX.pin2, SON.pin2, BLUETOOTH.pin3, DIST.pin3, BATTERIE.+, HP.pin2, RBPLAY.Pin_1, RBLUX.Pin_1, RBSON.Pin_1, RLSON.Pin_1, RBATTERIE2.Pin_0, RBDIST.Pin_1, RLLUX.Pin_1
  N1: NANO.D2, 7_SEGMENTS.pin3
  N2: NANO.D3, 7_SEGMENTS.pin4
  N3: NANO.D4, RBPLAY.Pin_0, BPLAY.Pin_1
  N4: NANO.D5, RBLUX.Pin_0, BLUX.Pin_1
  N5: NANO.D6, BDIST.Pin_1, RBDIST.Pin_0
  N6: NANO.D7, RBSON.Pin_0, BSON.Pin_1
  N7: NANO.D8, LED_LUX.cathode
  N8: NANO.D9, LED_DIST.cathode, POINTEUR.pin1
  N9: NANO.D10, LED_SON.cathode
  N10: NANO.VIN, BATTERIE.-, RBATTERIE.Pin_1
  5V: NANO.5V, 7_SEGMENTS.pin2, POINTEUR.pin2, LUX.pin3, SON.pin3, BLUETOOTH.pin4, DIST.pin4, BSON.Pin_2, BDIST.Pin_2, BLUX.Pin_2, BPLAY.Pin_2
  N11: NANO.A7, HP.pin1
  N12: NANO.A6, BLUETOOTH.pin1
  N13: NANO.A5, BLUETOOTH.pin2
  N14: NANO.A4, DIST.pin1
  N15: NANO.A3, DIST.pin2
  N16: NANO.A2, SON.pin1
  N17: NANO.A1, LUX.pin1
  N18: NANO.A0, RBATTERIE2.Pin_1, RBATTERIE.Pin_0
  N19: LED_SON.anode, RLSON.Pin_0
  N20: LED_LUX.anode, RLLUX.Pin_0

notes:
  DTY MCAS TOP
  DTY MCAS BOT
